// Logisim project Processor.circ as structural Verilog: 28 circuits, main circuit ALU
module main (
  input  B1,
  input  [9:0] in_2
);

  wire clock_1_out, control_unit_1_p5, control_unit_1_p6, control_unit_1_p7, control_unit_1_p8,
       control_unit_1_p9, control_unit_1_p10, control_unit_1_p11, control_unit_1_p12, control_unit_1_p13;
  wire [2:0] control_unit_1_p4;
  wire [3:0] SRC1, SRC2;
  wire [9:0] pc_1_output;
  wire [19:0] REG1, REG2, rom_1_data;

  PC pc_1 (.Enable(B1), .Input(in_2), .Clock(clock_1_out), .Write(1'b1), .Output(pc_1_output));
  Clock clock_1 (.out(clock_1_out));
  ROM #(.addrWidth(10), .dataWidth(20)) rom_1 (.addr(pc_1_output), .data(rom_1_data), .sel(1'b1));
  // Control_Unit control_unit_1: pin names not known; wires that end beside it: rom_1_data, SRC1, SRC2, control_unit_1_p4, control_unit_1_p5, control_unit_1_p6, control_unit_1_p7, control_unit_1_p8, control_unit_1_p9, control_unit_1_p10, control_unit_1_p11, control_unit_1_p12, control_unit_1_p13
  ALU alu_1 (.A(REG1), .Clock(clock_1_out), .B(REG2), .OPCODE(control_unit_1_p4));  // open: in_5, out_6, out_7
  RegisterFile registerfile_1 (
    .ReadRegister1(SRC1), .ReadRegister2(SRC2), .Clock(clock_1_out), .out_7(REG1), .out_8(REG2));  // open: WriteData, WriteRegister, Write_Enable
  RAM #(.addrWidth(10), .dataWidth(20)) ram_1 ();  // open: addr, data, sel, clk, ld, clr

  // Notes on the sheet:
  //   Instruction Memory
  //   contents of rom_1 (hex, n*v repeats v):
  //   8005 0 10885 911 19101 1222 21985 1b33 2a20c 2444 30005 303fb 3a80c 3b40f 5e00a 9e00f fc800 fd001
  //   Data Memory
endmodule

module ALU (
  input  [19:0] A,
  input  Clock,
  input  [19:0] B,
  input  [2:0] OPCODE,
  input  in_5,
  output [19:0] out_6,
  output out_7
);

  wire n20_bit_adder_1_out_5, n20_bit_subtractor_1_out_5;
  wire [19:0] and_1_out, n20_bit_adder_1_out_4, n20_bit_subtractor_1_out_4, or_1_out, xor_1_out;

  assign and_1_out = A & B;  // AND_Gate and_1, 20 bits wide
  assign or_1_out = A | B;  // OR_Gate or_1, 20 bits wide
  assign xor_1_out = A ^ B;  // XOR_Gate xor_1, 20 bits wide
  _20_Bit_Adder u_20_bit_adder_1 (
    .in_1(A), .in_2(Clock), .in_3(B), .out_4(n20_bit_adder_1_out_4), .out_5(n20_bit_adder_1_out_5));
  _20_Bit_Subtractor u_20_bit_subtractor_1 (
    .in_1(A), .in_2(Clock), .in_3(B), .out_4(n20_bit_subtractor_1_out_4), .out_5(n20_bit_subtractor_1_out_5));
  Multiplexer #(.enable("false")) multiplexer_1 (
    .in0(n20_bit_adder_1_out_5), .in1(n20_bit_subtractor_1_out_5), .out(out_7), .sel(in_5));
  Multiplexer #(.select(3), .width(20), .enable("false")) multiplexer_2 (
    .in0(and_1_out), .in1(or_1_out), .in2(xor_1_out), .in3(n20_bit_adder_1_out_4),
    .in4(n20_bit_subtractor_1_out_4), .out(out_6), .sel(OPCODE));  // open: in5, in6, in7
endmodule

module Full_Adder (
  input  A,
  input  B,
  input  C,
  output SUM,
  output Carry_Out
);

  wire and_1_out, and_2_out, xor_1_out;

  xor xor_1 (xor_1_out, A, B);
  and and_1 (and_1_out, A, B);
  and and_2 (and_2_out, xor_1_out, C);
  xor xor_2 (SUM, xor_1_out, C);
  or or_1 (Carry_Out, and_2_out, and_1_out);
endmodule

module Half_Adder (
  input  A,
  input  B,
  output S,
  output C
);

  xor xor_1 (S, A, B);
  and and_1 (C, A, B);
endmodule

module _2_Bit_Adder (
  input  [1:0] in_1,
  input  Carry_In,
  input  [1:0] in_3,
  output [1:0] out_4,
  output Carry_Out
);

  wire full_adder_1_carry_out;

  Full_Adder full_adder_1 (.A(in_1[0]), .B(in_3[0]), .C(Carry_In), .SUM(out_4[0]), .Carry_Out(full_adder_1_carry_out));
  Full_Adder full_adder_2 (.A(in_1[1]), .B(in_3[1]), .C(full_adder_1_carry_out), .SUM(out_4[1]), .Carry_Out(Carry_Out));
endmodule

module _4_Bit_Adder (
  input  [3:0] in_1,
  input  in_2,
  input  [3:0] in_3,
  output [3:0] out_4,
  output out_5
);

  wire n2_bit_adder_1_carry_out;

  _2_Bit_Adder u_2_bit_adder_1 (
    .in_1(in_1[1:0]), .Carry_In(in_2), .in_3(in_3[1:0]), .out_4(out_4[1:0]),
    .Carry_Out(n2_bit_adder_1_carry_out));
  _2_Bit_Adder u_2_bit_adder_2 (
    .in_1(in_1[3:2]), .Carry_In(n2_bit_adder_1_carry_out), .in_3(in_3[3:2]), .out_4(out_4[3:2]),
    .Carry_Out(out_5));
endmodule

module _8_Bit_Adder (
  input  [7:0] in_1,
  input  in_2,
  input  [7:0] in_3,
  output [7:0] out_4,
  output out_5
);

  wire n4_bit_adder_1_out_5;

  _4_Bit_Adder u_4_bit_adder_1 (
    .in_1(in_1[3:0]), .in_2(in_2), .in_3(in_3[3:0]), .out_4(out_4[3:0]), .out_5(n4_bit_adder_1_out_5));
  _4_Bit_Adder u_4_bit_adder_2 (
    .in_1(in_1[7:4]), .in_2(n4_bit_adder_1_out_5), .in_3(in_3[7:4]), .out_4(out_4[7:4]), .out_5(out_5));
endmodule

module _16_Bit_Adder (
  input  [15:0] in_1,
  input  in_2,
  input  [15:0] in_3,
  output [15:0] out_4,
  output out_5
);

  wire n8_bit_adder_1_out_5;

  _8_Bit_Adder u_8_bit_adder_1 (
    .in_1(in_1[7:0]), .in_2(in_2), .in_3(in_3[7:0]), .out_4(out_4[7:0]), .out_5(n8_bit_adder_1_out_5));
  _8_Bit_Adder u_8_bit_adder_2 (
    .in_1(in_1[15:8]), .in_2(n8_bit_adder_1_out_5), .in_3(in_3[15:8]), .out_4(out_4[15:8]), .out_5(out_5));
endmodule

module Full_Subtractor (
  input  A,
  input  B,
  input  C,
  output out_4,
  output out_5
);

  wire and_1_out, and_2_out, and_3_out, not_1_out, or_1_out, xor_1_out;

  not not_1 (not_1_out, A);
  and and_1 (and_1_out, not_1_out, B);
  and and_2 (and_2_out, not_1_out, C);
  xor xor_1 (xor_1_out, A, B);
  or or_1 (or_1_out, and_1_out, and_2_out);
  and and_3 (and_3_out, C, B);
  xor xor_2 (out_4, xor_1_out, C);
  or or_2 (out_5, or_1_out, and_3_out);
endmodule

module _2_Bit_Subtractor (
  input  [1:0] in_1,
  input  Carry_In,
  input  [1:0] in_3,
  output [1:0] out_4,
  output Carry_Out
);

  wire full_subtractor_1_out_5;

  Full_Subtractor full_subtractor_1 (
    .A(in_1[0]), .B(in_3[0]), .C(Carry_In), .out_4(out_4[0]), .out_5(full_subtractor_1_out_5));
  Full_Subtractor full_subtractor_2 (
    .A(in_1[1]), .B(in_3[1]), .C(full_subtractor_1_out_5), .out_4(out_4[1]), .out_5(Carry_Out));
endmodule

module _4_Bit_Subtractor (
  input  [3:0] in_1,
  input  in_2,
  input  [3:0] in_3,
  output [3:0] out_4,
  output out_5
);

  wire n2_bit_subtractor_1_carry_out;

  _2_Bit_Subtractor u_2_bit_subtractor_1 (
    .in_1(in_1[1:0]), .Carry_In(in_2), .in_3(in_3[1:0]), .out_4(out_4[1:0]),
    .Carry_Out(n2_bit_subtractor_1_carry_out));
  _2_Bit_Subtractor u_2_bit_subtractor_2 (
    .in_1(in_1[3:2]), .Carry_In(n2_bit_subtractor_1_carry_out), .in_3(in_3[3:2]), .out_4(out_4[3:2]),
    .Carry_Out(out_5));
endmodule

module _8_Bit_Subtractor (
  input  [7:0] in_1,
  input  in_2,
  input  [7:0] in_3,
  output [7:0] out_4,
  output out_5
);

  wire n4_bit_subtractor_1_out_5;

  _4_Bit_Subtractor u_4_bit_subtractor_1 (
    .in_1(in_1[3:0]), .in_2(in_2), .in_3(in_3[3:0]), .out_4(out_4[3:0]), .out_5(n4_bit_subtractor_1_out_5));
  _4_Bit_Subtractor u_4_bit_subtractor_2 (
    .in_1(in_1[7:4]), .in_2(n4_bit_subtractor_1_out_5), .in_3(in_3[7:4]), .out_4(out_4[7:4]), .out_5(out_5));
endmodule

module _16_Bit_Subtractor (
  input  [15:0] in_1,
  input  in_2,
  input  [15:0] in_3,
  output [15:0] out_4,
  output out_5
);

  wire n8_bit_subtractor_1_out_5;

  _8_Bit_Subtractor u_8_bit_subtractor_1 (
    .in_1(in_1[7:0]), .in_2(in_2), .in_3(in_3[7:0]), .out_4(out_4[7:0]), .out_5(n8_bit_subtractor_1_out_5));
  _8_Bit_Subtractor u_8_bit_subtractor_2 (
    .in_1(in_1[15:8]), .in_2(n8_bit_subtractor_1_out_5), .in_3(in_3[15:8]), .out_4(out_4[15:8]), .out_5(out_5));
endmodule

module _20_Bit_Adder (
  input  [19:0] in_1,
  input  in_2,
  input  [19:0] in_3,
  output [19:0] out_4,
  output out_5
);

  wire n16_bit_adder_1_out_5;

  _16_Bit_Adder u_16_bit_adder_1 (
    .in_1(in_1[15:0]), .in_2(in_2), .in_3(in_3[15:0]), .out_4(out_4[15:0]), .out_5(n16_bit_adder_1_out_5));
  _4_Bit_Adder u_4_bit_adder_1 (
    .in_1(in_1[19:16]), .in_2(n16_bit_adder_1_out_5), .in_3(in_3[19:16]), .out_4(out_4[19:16]), .out_5(out_5));
endmodule

module RegisterFile (
  input  [3:0] ReadRegister1,
  input  [19:0] WriteData,
  input  [3:0] WriteRegister,
  input  [3:0] ReadRegister2,
  input  Clock,
  input  Write_Enable,
  output [19:0] out_7,
  output [19:0] out_8
);

  wire and_1_out, and_2_out, and_3_out, and_4_out, and_5_out, and_6_out, and_7_out, and_8_out, and_9_out,
       and_10_out, and_11_out, and_12_out, and_13_out, and_14_out, and_15_out, and_16_out, decoder_1_out0,
       decoder_1_out1, decoder_1_out2, decoder_1_out3, decoder_1_out4, decoder_1_out5, decoder_1_out6,
       decoder_1_out7, decoder_1_out8, decoder_1_out9, decoder_1_out10, decoder_1_out11, decoder_1_out12,
       decoder_1_out13, decoder_1_out14, decoder_1_out15, decoder_2_out0, decoder_2_out1, decoder_2_out2,
       decoder_2_out3, decoder_2_out4, decoder_2_out5, decoder_2_out6, decoder_2_out7, decoder_2_out8,
       decoder_2_out9, decoder_2_out10, decoder_2_out11, decoder_2_out12, decoder_2_out13, decoder_2_out14,
       decoder_2_out15, decoder_3_out0, decoder_3_out1, decoder_3_out2, decoder_3_out3, decoder_3_out4,
       decoder_3_out5, decoder_3_out6, decoder_3_out7, decoder_3_out8, decoder_3_out9, decoder_3_out10,
       decoder_3_out11, decoder_3_out12, decoder_3_out13, decoder_3_out14, decoder_3_out15;
  wire [19:0] n20_bit_register_1_out_4, n20_bit_register_2_out_4, n20_bit_register_3_out_4,
       n20_bit_register_4_out_4, n20_bit_register_5_out_4, n20_bit_register_6_out_4,
       n20_bit_register_7_out_4, n20_bit_register_8_out_4, n20_bit_register_9_out_4,
       n20_bit_register_10_out_4, n20_bit_register_11_out_4, n20_bit_register_12_out_4,
       n20_bit_register_13_out_4, n20_bit_register_14_out_4, n20_bit_register_15_out_4,
       n20_bit_register_16_out_4;

  Decoder #(.select(4), .enable("false")) decoder_1 (
    .out0(decoder_1_out0), .out1(decoder_1_out1), .out2(decoder_1_out2), .out3(decoder_1_out3),
    .out4(decoder_1_out4), .out5(decoder_1_out5), .out6(decoder_1_out6), .out7(decoder_1_out7),
    .out8(decoder_1_out8), .out9(decoder_1_out9), .out10(decoder_1_out10), .out11(decoder_1_out11),
    .out12(decoder_1_out12), .out13(decoder_1_out13), .out14(decoder_1_out14), .out15(decoder_1_out15),
    .sel(ReadRegister1));
  Decoder #(.select(4), .enable("false")) decoder_2 (
    .out0(decoder_2_out0), .out1(decoder_2_out1), .out2(decoder_2_out2), .out3(decoder_2_out3),
    .out4(decoder_2_out4), .out5(decoder_2_out5), .out6(decoder_2_out6), .out7(decoder_2_out7),
    .out8(decoder_2_out8), .out9(decoder_2_out9), .out10(decoder_2_out10), .out11(decoder_2_out11),
    .out12(decoder_2_out12), .out13(decoder_2_out13), .out14(decoder_2_out14), .out15(decoder_2_out15),
    .sel(WriteRegister));
  Decoder #(.select(4), .enable("false")) decoder_3 (
    .out0(decoder_3_out0), .out1(decoder_3_out1), .out2(decoder_3_out2), .out3(decoder_3_out3),
    .out4(decoder_3_out4), .out5(decoder_3_out5), .out6(decoder_3_out6), .out7(decoder_3_out7),
    .out8(decoder_3_out8), .out9(decoder_3_out9), .out10(decoder_3_out10), .out11(decoder_3_out11),
    .out12(decoder_3_out12), .out13(decoder_3_out13), .out14(decoder_3_out14), .out15(decoder_3_out15),
    .sel(ReadRegister2));
  and and_1 (and_1_out, decoder_2_out0, Write_Enable);
  and and_2 (and_2_out, decoder_2_out1, Write_Enable);
  and and_3 (and_3_out, decoder_2_out2, Write_Enable);
  and and_4 (and_4_out, decoder_2_out3, Write_Enable);
  and and_5 (and_5_out, decoder_2_out4, Write_Enable);
  and and_6 (and_6_out, decoder_2_out5, Write_Enable);
  and and_7 (and_7_out, decoder_2_out6, Write_Enable);
  and and_8 (and_8_out, decoder_2_out7, Write_Enable);
  _20_Bit_Register u_20_bit_register_1 (
    .in_1(WriteData), .Enable(and_1_out), .out_4(n20_bit_register_1_out_4), .Clock(Clock));
  _20_Bit_Register u_20_bit_register_2 (
    .in_1(WriteData), .Enable(and_2_out), .out_4(n20_bit_register_2_out_4), .Clock(Clock));
  _20_Bit_Register u_20_bit_register_3 (
    .in_1(WriteData), .Enable(and_3_out), .out_4(n20_bit_register_3_out_4), .Clock(Clock));
  _20_Bit_Register u_20_bit_register_4 (
    .in_1(WriteData), .Enable(and_4_out), .out_4(n20_bit_register_4_out_4), .Clock(Clock));
  _20_Bit_Register u_20_bit_register_5 (
    .in_1(WriteData), .Enable(and_5_out), .out_4(n20_bit_register_5_out_4), .Clock(Clock));
  _20_Bit_Register u_20_bit_register_6 (
    .in_1(WriteData), .Enable(and_6_out), .out_4(n20_bit_register_6_out_4), .Clock(Clock));
  _20_Bit_Register u_20_bit_register_7 (
    .in_1(WriteData), .Enable(and_7_out), .out_4(n20_bit_register_7_out_4), .Clock(Clock));
  _20_Bit_Register u_20_bit_register_8 (
    .in_1(WriteData), .Enable(and_8_out), .out_4(n20_bit_register_8_out_4), .Clock(Clock));
  and and_9 (and_9_out, decoder_2_out8, Write_Enable);
  and and_10 (and_10_out, decoder_2_out9, Write_Enable);
  and and_11 (and_11_out, decoder_2_out10, Write_Enable);
  and and_12 (and_12_out, decoder_2_out11, Write_Enable);
  and and_13 (and_13_out, decoder_2_out12, Write_Enable);
  and and_14 (and_14_out, decoder_2_out13, Write_Enable);
  and and_15 (and_15_out, decoder_2_out14, Write_Enable);
  and and_16 (and_16_out, decoder_2_out15, Write_Enable);
  assign out_8 = decoder_3_out0 ? n20_bit_register_1_out_4 : 20'bz;  // Controlled_Buffer controlled_buffer_1
  _20_Bit_Register u_20_bit_register_9 (
    .in_1(WriteData), .Enable(and_9_out), .out_4(n20_bit_register_9_out_4), .Clock(Clock));
  assign out_8 = decoder_3_out1 ? n20_bit_register_2_out_4 : 20'bz;  // Controlled_Buffer controlled_buffer_2
  _20_Bit_Register u_20_bit_register_10 (
    .in_1(WriteData), .Enable(and_10_out), .out_4(n20_bit_register_10_out_4), .Clock(Clock));
  _20_Bit_Register u_20_bit_register_11 (
    .in_1(WriteData), .Enable(and_11_out), .out_4(n20_bit_register_11_out_4), .Clock(Clock));
  _20_Bit_Register u_20_bit_register_12 (
    .in_1(WriteData), .Enable(and_12_out), .out_4(n20_bit_register_12_out_4), .Clock(Clock));
  _20_Bit_Register u_20_bit_register_13 (
    .in_1(WriteData), .Enable(and_13_out), .out_4(n20_bit_register_13_out_4), .Clock(Clock));
  _20_Bit_Register u_20_bit_register_14 (
    .in_1(WriteData), .Enable(and_14_out), .out_4(n20_bit_register_14_out_4), .Clock(Clock));
  _20_Bit_Register u_20_bit_register_15 (
    .in_1(WriteData), .Enable(and_15_out), .out_4(n20_bit_register_15_out_4), .Clock(Clock));
  _20_Bit_Register u_20_bit_register_16 (
    .in_1(WriteData), .Enable(and_16_out), .out_4(n20_bit_register_16_out_4), .Clock(Clock));
  assign out_7 = decoder_1_out0 ? n20_bit_register_1_out_4 : 20'bz;  // Controlled_Buffer controlled_buffer_3
  assign out_7 = decoder_1_out1 ? n20_bit_register_2_out_4 : 20'bz;  // Controlled_Buffer controlled_buffer_4
  assign out_7 = decoder_1_out2 ? n20_bit_register_3_out_4 : 20'bz;  // Controlled_Buffer controlled_buffer_5
  assign out_8 = decoder_3_out2 ? n20_bit_register_3_out_4 : 20'bz;  // Controlled_Buffer controlled_buffer_6
  assign out_7 = decoder_1_out3 ? n20_bit_register_4_out_4 : 20'bz;  // Controlled_Buffer controlled_buffer_7
  assign out_8 = decoder_3_out3 ? n20_bit_register_4_out_4 : 20'bz;  // Controlled_Buffer controlled_buffer_8
  Controlled_Buffer #(.width(20)) controlled_buffer_9 (
    .in(n20_bit_register_5_out_4), .en(decoder_3_out4));  // open: out
  assign out_8 = decoder_3_out5 ? n20_bit_register_6_out_4 : 20'bz;  // Controlled_Buffer controlled_buffer_10
  assign out_7 = decoder_1_out4 ? n20_bit_register_5_out_4 : 20'bz;  // Controlled_Buffer controlled_buffer_11
  assign out_7 = decoder_1_out5 ? n20_bit_register_6_out_4 : 20'bz;  // Controlled_Buffer controlled_buffer_12
  assign out_7 = decoder_1_out6 ? n20_bit_register_7_out_4 : 20'bz;  // Controlled_Buffer controlled_buffer_13
  assign out_8 = decoder_3_out6 ? n20_bit_register_7_out_4 : 20'bz;  // Controlled_Buffer controlled_buffer_14
  assign out_7 = decoder_1_out7 ? n20_bit_register_8_out_4 : 20'bz;  // Controlled_Buffer controlled_buffer_15
  assign out_8 = decoder_3_out7 ? n20_bit_register_8_out_4 : 20'bz;  // Controlled_Buffer controlled_buffer_16
  assign out_7 = decoder_1_out8 ? n20_bit_register_9_out_4 : 20'bz;  // Controlled_Buffer controlled_buffer_17
  assign out_8 = decoder_3_out8 ? n20_bit_register_9_out_4 : 20'bz;  // Controlled_Buffer controlled_buffer_18
  assign out_7 = decoder_1_out9 ? n20_bit_register_10_out_4 : 20'bz;  // Controlled_Buffer controlled_buffer_19
  assign out_8 = decoder_3_out9 ? n20_bit_register_10_out_4 : 20'bz;  // Controlled_Buffer controlled_buffer_20
  assign out_7 = decoder_1_out10 ? n20_bit_register_11_out_4 : 20'bz;  // Controlled_Buffer controlled_buffer_21
  assign out_8 = decoder_3_out10 ? n20_bit_register_11_out_4 : 20'bz;  // Controlled_Buffer controlled_buffer_22
  assign out_7 = decoder_1_out11 ? n20_bit_register_12_out_4 : 20'bz;  // Controlled_Buffer controlled_buffer_23
  assign out_8 = decoder_3_out11 ? n20_bit_register_12_out_4 : 20'bz;  // Controlled_Buffer controlled_buffer_24
  assign out_7 = decoder_1_out12 ? n20_bit_register_13_out_4 : 20'bz;  // Controlled_Buffer controlled_buffer_25
  assign out_8 = decoder_3_out12 ? n20_bit_register_13_out_4 : 20'bz;  // Controlled_Buffer controlled_buffer_26
  assign out_7 = decoder_1_out13 ? n20_bit_register_14_out_4 : 20'bz;  // Controlled_Buffer controlled_buffer_27
  assign out_8 = decoder_3_out13 ? n20_bit_register_14_out_4 : 20'bz;  // Controlled_Buffer controlled_buffer_28
  assign out_7 = decoder_1_out14 ? n20_bit_register_15_out_4 : 20'bz;  // Controlled_Buffer controlled_buffer_29
  assign out_8 = decoder_3_out14 ? n20_bit_register_15_out_4 : 20'bz;  // Controlled_Buffer controlled_buffer_30
  assign out_7 = decoder_1_out15 ? n20_bit_register_16_out_4 : 20'bz;  // Controlled_Buffer controlled_buffer_31
  assign out_8 = decoder_3_out15 ? n20_bit_register_16_out_4 : 20'bz;  // Controlled_Buffer controlled_buffer_32
endmodule

module d_Latch (
  input  D,
  input  C,
  output Q
);

  wire and_1_out, and_2_out, nor_1_out;

  and and_1 (and_1_out, D, C);
  and and_2 (and_2_out, C, ~D);  // AND_Gate
  nor nor_1 (nor_1_out, and_1_out, Q);
  nor nor_2 (Q, nor_1_out, and_2_out);
endmodule

module d_Flip_Flop (
  input  D,
  input  clk,
  output Q
);

  wire d_latch_1_q, not_1_out;

  d_Latch d_latch_1 (.D(D), .C(not_1_out), .Q(d_latch_1_q));
  not not_1 (not_1_out, clk);
  d_Latch d_latch_2 (.D(d_latch_1_q), .C(clk), .Q(Q));
endmodule

module _20_Bit_Register (
  input  [19:0] in_1,
  input  Enable,
  input  Clock,
  output [19:0] out_4
);

  wire and_1_out, and_2_out, and_3_out, and_4_out, and_5_out, and_6_out, and_7_out, and_8_out, and_9_out,
       and_10_out, and_11_out, and_12_out, and_13_out, and_14_out, and_15_out, and_16_out, and_17_out,
       and_18_out, and_19_out, and_20_out;

  and and_1 (and_1_out, in_1[0], Enable);
  and and_2 (and_2_out, in_1[1], Enable);
  and and_3 (and_3_out, in_1[2], Enable);
  and and_4 (and_4_out, in_1[3], Enable);
  and and_5 (and_5_out, in_1[4], Enable);
  and and_6 (and_6_out, in_1[5], Enable);
  and and_7 (and_7_out, in_1[6], Enable);
  and and_8 (and_8_out, in_1[7], Enable);
  and and_9 (and_9_out, in_1[8], Enable);
  and and_10 (and_10_out, in_1[9], Enable);
  and and_11 (and_11_out, in_1[10], Enable);
  and and_12 (and_12_out, in_1[11], Enable);
  and and_13 (and_13_out, in_1[12], Enable);
  and and_14 (and_14_out, in_1[13], Enable);
  and and_15 (and_15_out, in_1[14], Enable);
  and and_16 (and_16_out, in_1[15], Enable);
  and and_17 (and_17_out, in_1[16], Enable);
  and and_18 (and_18_out, in_1[17], Enable);
  and and_19 (and_19_out, in_1[18], Enable);
  and and_20 (and_20_out, in_1[19], Enable);
  d_Flip_Flop d_flip_flop_1 (.D(and_1_out), .clk(Clock), .Q(out_4[0]));
  d_Flip_Flop d_flip_flop_2 (.D(and_2_out), .clk(Clock), .Q(out_4[1]));
  d_Flip_Flop d_flip_flop_3 (.D(and_3_out), .clk(Clock), .Q(out_4[2]));
  d_Flip_Flop d_flip_flop_4 (.D(and_4_out), .clk(Clock), .Q(out_4[3]));
  d_Flip_Flop d_flip_flop_5 (.D(and_5_out), .clk(Clock), .Q(out_4[4]));
  d_Flip_Flop d_flip_flop_6 (.D(and_6_out), .clk(Clock), .Q(out_4[5]));
  d_Flip_Flop d_flip_flop_7 (.D(and_7_out), .clk(Clock), .Q(out_4[6]));
  d_Flip_Flop d_flip_flop_8 (.D(and_8_out), .clk(Clock), .Q(out_4[7]));
  d_Flip_Flop d_flip_flop_9 (.D(and_9_out), .clk(Clock), .Q(out_4[8]));
  d_Flip_Flop d_flip_flop_10 (.D(and_10_out), .clk(Clock), .Q(out_4[9]));
  d_Flip_Flop d_flip_flop_11 (.D(and_11_out), .clk(Clock), .Q(out_4[10]));
  d_Flip_Flop d_flip_flop_12 (.D(and_12_out), .clk(Clock), .Q(out_4[11]));
  d_Flip_Flop d_flip_flop_13 (.D(and_13_out), .clk(Clock), .Q(out_4[12]));
  d_Flip_Flop d_flip_flop_14 (.D(and_14_out), .clk(Clock), .Q(out_4[13]));
  d_Flip_Flop d_flip_flop_15 (.D(and_15_out), .clk(Clock), .Q(out_4[14]));
  d_Flip_Flop d_flip_flop_16 (.D(and_16_out), .clk(Clock), .Q(out_4[15]));
  d_Flip_Flop d_flip_flop_17 (.D(and_17_out), .clk(Clock), .Q(out_4[16]));
  d_Flip_Flop d_flip_flop_18 (.D(and_18_out), .clk(Clock), .Q(out_4[17]));
  d_Flip_Flop d_flip_flop_19 (.D(and_19_out), .clk(Clock), .Q(out_4[18]));
  d_Flip_Flop d_flip_flop_20 (.D(and_20_out), .clk(Clock), .Q(out_4[19]));
endmodule

module _20_Bit_Subtractor (
  input  [19:0] in_1,
  input  in_2,
  input  [19:0] in_3,
  output [19:0] out_4,
  output out_5
);

  wire n16_bit_subtractor_1_out_5;

  _16_Bit_Subtractor u_16_bit_subtractor_1 (
    .in_1(in_1[15:0]), .in_2(in_2), .in_3(in_3[15:0]), .out_4(out_4[15:0]), .out_5(n16_bit_subtractor_1_out_5));
  _4_Bit_Subtractor u_4_bit_subtractor_1 (
    .in_1(in_1[19:16]), .in_2(n16_bit_subtractor_1_out_5), .in_3(in_3[19:16]), .out_4(out_4[19:16]),
    .out_5(out_5));
endmodule

module PC (
  input  Enable,
  input  [9:0] Input,
  input  Write,
  input  Clock,
  output [9:0] Output
);

  wire not_1_out;
  wire [9:0] controlled_buffer_1_out, n10_bit_adder_1_output;

  not not_1 (not_1_out, Enable);
  assign controlled_buffer_1_out = Enable ? Input : 10'bz;  // Controlled_Buffer controlled_buffer_1
  assign controlled_buffer_1_out = not_1_out ? n10_bit_adder_1_output : 10'bz;  // Controlled_Buffer controlled_buffer_2
  _10_Bit_Register u_10_bit_register_1 (.in_1(controlled_buffer_1_out), .Enable(Write), .Clock(Clock), .out_4(Output));
  _10_Bit_Adder u_10_bit_adder_1 (
    .Value_1(Output), .C_In(1'b1), .Value_2({10{1'b0}}), .Output(n10_bit_adder_1_output));  // open: C_Out
endmodule

module _10_Bit_Register (
  input  [9:0] in_1,
  input  Clock,
  input  Enable,
  output [9:0] out_4
);

  wire and_1_out, and_2_out, and_3_out, and_4_out, and_5_out, and_6_out, and_7_out, and_8_out, and_9_out,
       and_10_out;

  and and_1 (and_1_out, in_1[0], Enable);
  and and_2 (and_2_out, in_1[1], Enable);
  and and_3 (and_3_out, in_1[2], Enable);
  and and_4 (and_4_out, in_1[3], Enable);
  and and_5 (and_5_out, in_1[4], Enable);
  and and_6 (and_6_out, in_1[5], Enable);
  and and_7 (and_7_out, in_1[6], Enable);
  and and_8 (and_8_out, in_1[7], Enable);
  and and_9 (and_9_out, in_1[8], Enable);
  and and_10 (and_10_out, in_1[9], Enable);
  d_Flip_Flop d_flip_flop_1 (.D(and_1_out), .clk(Clock), .Q(out_4[0]));
  d_Flip_Flop d_flip_flop_2 (.D(and_2_out), .clk(Clock), .Q(out_4[1]));
  d_Flip_Flop d_flip_flop_3 (.D(and_3_out), .clk(Clock), .Q(out_4[2]));
  d_Flip_Flop d_flip_flop_4 (.D(and_4_out), .clk(Clock), .Q(out_4[3]));
  d_Flip_Flop d_flip_flop_5 (.D(and_5_out), .clk(Clock), .Q(out_4[4]));
  d_Flip_Flop d_flip_flop_6 (.D(and_6_out), .clk(Clock), .Q(out_4[5]));
  d_Flip_Flop d_flip_flop_7 (.D(and_7_out), .clk(Clock), .Q(out_4[6]));
  d_Flip_Flop d_flip_flop_8 (.D(and_8_out), .clk(Clock), .Q(out_4[7]));
  d_Flip_Flop d_flip_flop_9 (.D(and_9_out), .clk(Clock), .Q(out_4[8]));
  d_Flip_Flop d_flip_flop_10 (.D(and_10_out), .clk(Clock), .Q(out_4[9]));
endmodule

module _10_Bit_Adder (
  input  [9:0] Value_1,
  input  C_In,
  input  [9:0] Value_2,
  output [9:0] Output,
  output C_Out
);

  wire n8_bit_adder_1_out_5;

  _8_Bit_Adder u_8_bit_adder_1 (
    .in_1(Value_1[7:0]), .in_2(C_In), .in_3(Value_2[7:0]), .out_4(Output[7:0]), .out_5(n8_bit_adder_1_out_5));
  _2_Bit_Adder u_2_bit_adder_1 (
    .in_1(Value_1[9:8]), .Carry_In(n8_bit_adder_1_out_5), .in_3(Value_2[9:8]), .out_4(Output[9:8]),
    .Carry_Out(C_Out));
endmodule

module _2_Bit_Comparator (
  input  A1,
  input  A0,
  input  B1,
  input  B0,
  output A___B,
  output A___B_2,
  output A___B_3
);

  wire and_1_out, and_2_out, and_3_out, and_4_out, and_5_out, and_6_out, not_1_out, not_2_out, not_3_out,
       not_4_out, xnor_1_out, xnor_2_out;

  not not_1 (not_1_out, A1);
  not not_2 (not_2_out, A0);
  not not_3 (not_3_out, B1);
  not not_4 (not_4_out, B0);
  and and_1 (and_1_out, not_1_out, B1);
  and and_2 (and_2_out, not_2_out, B1, B0);
  and and_3 (and_3_out, not_1_out, not_2_out, B0);
  xnor xnor_1 (xnor_1_out, A1, B1);
  xnor xnor_2 (xnor_2_out, A0, B0);
  and and_4 (and_4_out, A1, not_3_out);
  and and_5 (and_5_out, A0, not_3_out, not_4_out);
  and and_6 (and_6_out, A1, A0, not_4_out);
  or or_1 (A___B, and_1_out, and_2_out, and_3_out);
  and and_7 (A___B_2, xnor_1_out, xnor_2_out);
  or or_2 (A___B_3, and_4_out, and_5_out, and_6_out);
endmodule

module _4_Bit_Comparator (
  input  A3,
  input  A2,
  input  A1,
  input  A0,
  input  B3,
  input  B2,
  input  B1,
  input  B0,
  output A___B,
  output A___B_2,
  output A___B_3
);

  wire and_1_out, and_2_out, n2_bit_comparator_1_a___b, n2_bit_comparator_1_a___b_2,
       n2_bit_comparator_1_a___b_3, n2_bit_comparator_2_a___b, n2_bit_comparator_2_a___b_2,
       n2_bit_comparator_2_a___b_3;

  _2_Bit_Comparator u_2_bit_comparator_1 (
    .A1(A3), .A0(A2), .B1(B3), .B0(B2), .A___B(n2_bit_comparator_1_a___b),
    .A___B_2(n2_bit_comparator_1_a___b_2), .A___B_3(n2_bit_comparator_1_a___b_3));
  _2_Bit_Comparator u_2_bit_comparator_2 (
    .A1(A1), .A0(A0), .B1(B1), .B0(B0), .A___B(n2_bit_comparator_2_a___b),
    .A___B_2(n2_bit_comparator_2_a___b_2), .A___B_3(n2_bit_comparator_2_a___b_3));
  and and_1 (and_1_out, n2_bit_comparator_1_a___b_2, n2_bit_comparator_2_a___b_3);
  and and_2 (and_2_out, n2_bit_comparator_1_a___b_2, n2_bit_comparator_2_a___b);
  and and_3 (A___B, n2_bit_comparator_1_a___b_2, n2_bit_comparator_2_a___b_2);
  or or_1 (A___B_2, n2_bit_comparator_1_a___b_3, and_1_out);
  or or_2 (A___B_3, and_2_out, n2_bit_comparator_1_a___b);
endmodule

module _8_Bit_Comparator (
  input  A7,
  input  A6,
  input  A5,
  input  A4,
  input  A3,
  input  A2,
  input  A1,
  input  A0,
  input  B7,
  input  B6,
  input  B5,
  input  B4,
  input  B3,
  input  B2,
  input  B1,
  input  B0,
  output A___B,
  output A___B_2,
  output A___B_3
);

  wire and_1_out, and_2_out, n4_bit_comparator_1_a___b, n4_bit_comparator_1_a___b_2,
       n4_bit_comparator_1_a___b_3, n4_bit_comparator_2_a___b, n4_bit_comparator_2_a___b_2,
       n4_bit_comparator_2_a___b_3;

  _4_Bit_Comparator u_4_bit_comparator_1 (
    .A3(A3), .A2(A2), .A1(A1), .A0(A0), .B3(B3), .B2(B2), .B1(B1), .B0(B0),
    .A___B(n4_bit_comparator_1_a___b), .A___B_2(n4_bit_comparator_1_a___b_2),
    .A___B_3(n4_bit_comparator_1_a___b_3));
  _4_Bit_Comparator u_4_bit_comparator_2 (
    .A3(A7), .A2(A6), .A1(A5), .A0(A4), .B3(B7), .B2(B6), .B1(B5), .B0(B4),
    .A___B(n4_bit_comparator_2_a___b), .A___B_2(n4_bit_comparator_2_a___b_2),
    .A___B_3(n4_bit_comparator_2_a___b_3));
  and and_1 (and_1_out, n4_bit_comparator_2_a___b, n4_bit_comparator_1_a___b_2);
  and and_2 (and_2_out, n4_bit_comparator_2_a___b, n4_bit_comparator_1_a___b_3);
  and and_3 (A___B, n4_bit_comparator_2_a___b, n4_bit_comparator_1_a___b);
  or or_1 (A___B_2, n4_bit_comparator_2_a___b_2, and_1_out);
  or or_2 (A___B_3, and_2_out, n4_bit_comparator_2_a___b_3);
endmodule

module _16_Bit_Comparator (
  input  A15,
  input  A14,
  input  A13,
  input  A12,
  input  A11,
  input  A10,
  input  A9,
  input  A8,
  input  A7,
  input  A6,
  input  A5,
  input  A4,
  input  A3,
  input  A2,
  input  A1,
  input  A0,
  input  B15,
  input  B14,
  input  B13,
  input  B12,
  input  B11,
  input  B10,
  input  B9,
  input  B8,
  input  B7,
  input  B6,
  input  B5,
  input  B4,
  input  B3,
  input  B2,
  input  B1,
  input  B0,
  output A___B,
  output A___B_2,
  output A___B_3
);

  wire and_1_out, and_2_out, n8_bit_comparator_1_a___b, n8_bit_comparator_1_a___b_2,
       n8_bit_comparator_1_a___b_3, n8_bit_comparator_2_a___b, n8_bit_comparator_2_a___b_2,
       n8_bit_comparator_2_a___b_3;

  _8_Bit_Comparator u_8_bit_comparator_1 (
    .A7(A7), .A6(A6), .A5(A5), .A4(A4), .A3(A3), .A2(A2), .A1(A1), .A0(A0), .B7(B7), .B6(B6), .B5(B5),
    .B4(B4), .B3(B3), .B2(B2), .B1(B1), .B0(B0), .A___B(n8_bit_comparator_1_a___b),
    .A___B_2(n8_bit_comparator_1_a___b_2), .A___B_3(n8_bit_comparator_1_a___b_3));
  and and_1 (and_1_out, n8_bit_comparator_2_a___b, n8_bit_comparator_1_a___b_2);
  and and_2 (and_2_out, n8_bit_comparator_2_a___b, n8_bit_comparator_1_a___b_3);
  and and_3 (A___B, n8_bit_comparator_2_a___b, n8_bit_comparator_1_a___b);
  or or_1 (A___B_2, n8_bit_comparator_2_a___b_2, and_1_out);
  or or_2 (A___B_3, and_2_out, n8_bit_comparator_2_a___b_3);
  _8_Bit_Comparator u_8_bit_comparator_2 (
    .A7(A15), .A6(A14), .A5(A13), .A4(A12), .A3(A11), .A2(A10), .A1(A9), .A0(A8), .B7(B15), .B6(B14),
    .B5(B13), .B4(B12), .B3(B11), .B2(B10), .B1(B9), .B0(B8), .A___B(n8_bit_comparator_2_a___b),
    .A___B_2(n8_bit_comparator_2_a___b_2), .A___B_3(n8_bit_comparator_2_a___b_3));
endmodule

module _20_Bit_Comparator (
  input  A19,
  input  A18,
  input  A17,
  input  A16,
  input  A15,
  input  A14,
  input  A13,
  input  A12,
  input  A11,
  input  A10,
  input  A9,
  input  A8,
  input  A7,
  input  A6,
  input  A5,
  input  A4,
  input  A3,
  input  A2,
  input  A1,
  input  A0,
  input  B19,
  input  B18,
  input  B17,
  input  B16,
  input  B15,
  input  B14,
  input  B13,
  input  B12,
  input  B11,
  input  B10,
  input  B9,
  input  B8,
  input  B7,
  input  B6,
  input  B5,
  input  B4,
  input  B3,
  input  B2,
  input  B1,
  input  B0,
  output A___B,
  output A___B_2,
  output A___B_3
);

  wire and_1_out, and_2_out, n4_bit_comparator_1_a___b, n4_bit_comparator_1_a___b_2,
       n4_bit_comparator_1_a___b_3, n16_bit_comparator_1_a___b, n16_bit_comparator_1_a___b_2,
       n16_bit_comparator_1_a___b_3;

  _16_Bit_Comparator u_16_bit_comparator_1 (
    .A15(A19), .A14(A18), .A13(A17), .A12(A16), .A11(A15), .A10(A14), .A9(A13), .A8(A12), .A7(A11), .A6(A10),
    .A5(A9), .A4(A8), .A3(A7), .A2(A6), .A1(A5), .A0(A4), .B15(B19), .B14(B18), .B13(B17), .B12(B16),
    .B11(B15), .B10(B14), .B9(B13), .B8(B12), .B7(B11), .B6(B10), .B5(B9), .B4(B8), .B3(B7), .B2(B6),
    .B1(B5), .B0(B4), .A___B(n16_bit_comparator_1_a___b), .A___B_2(n16_bit_comparator_1_a___b_2),
    .A___B_3(n16_bit_comparator_1_a___b_3));
  _4_Bit_Comparator u_4_bit_comparator_1 (
    .A3(A3), .A2(A2), .A1(A1), .A0(A0), .B3(B3), .B2(B2), .B1(B1), .B0(B0),
    .A___B(n4_bit_comparator_1_a___b), .A___B_2(n4_bit_comparator_1_a___b_2),
    .A___B_3(n4_bit_comparator_1_a___b_3));
  and and_1 (and_1_out, n16_bit_comparator_1_a___b, n4_bit_comparator_1_a___b_2);
  and and_2 (and_2_out, n16_bit_comparator_1_a___b, n4_bit_comparator_1_a___b_3);
  and and_3 (A___B, n16_bit_comparator_1_a___b, n4_bit_comparator_1_a___b);
  or or_1 (A___B_2, n16_bit_comparator_1_a___b_2, and_1_out);
  or or_2 (A___B_3, and_2_out, n16_bit_comparator_1_a___b_3);
endmodule

module Control_Unit (
  input  [19:0] in_1,
  output ADD,
  output SUB,
  output [3:0] SRC_1,
  output AND,
  output OR,
  output [3:0] SRC_2,
  output XOR,
  output [2:0] ALU_OPCODE,
  output ALU_ENABLE,
  output LD,
  output ST,
  output PUSH,
  output POP,
  output ADDI,
  output SUBI,
  output ANDI,
  output ORI,
  output XORI,
  output JUMP,
  output BE,
  output BNE
);

  wire LD__ST, PUSH__POP;

  Decoder #(.select(5), .enable("false")) decoder_1 (
    .out0(ALU_ENABLE), .out1(ADDI), .out2(SUBI), .out3(ANDI), .out4(ORI), .out5(XORI), .out6(JUMP),
    .out7(LD__ST), .out8(BE), .out16(BNE), .out31(PUSH__POP), .sel(in_1[19:15]));  // open: out9, out10, out11, out12, out13, out14, out15, out17, out18, out19, out20, out21, out22, out23, out24, out25, out26, out27, out28, out29, out30
  Decoder #(.select(3)) decoder_2 (
    .out0(ADD), .out1(SUB), .out2(AND), .out3(OR), .out4(XOR), .sel(in_1[10:8]), .en(ALU_ENABLE));  // open: out5, out6, out7
  Decoder decoder_3 (.out0(LD), .out1(ST), .sel(in_1[10]), .en(LD__ST));
  Decoder decoder_4 (.out0(PUSH), .out1(POP), .sel(in_1[0]), .en(PUSH__POP));

  assign ALU_OPCODE = in_1[10:8];
  assign SRC_1 = in_1[7:4];
  assign SRC_2 = in_1[3:0];

  // Other names for the same wires on the sheet: ADD__SUB__AND__OR__XOR = ALU_ENABLE; ADDR[9:0] = in_1[9:0];
  //   IMM[6:0] = in_1[6:0]; NULL2 = in_1[0]; SRC2[3:0] = in_1[3:0]; SRC1[3:0] = in_1[7:4]; SRC3[3:0] = in_1[10:7];
  //   NULL[2:0] = in_1[10:8]; Opcode[4:0] = in_1[19:15]; REG1[3:0] = in_1[17:14]; DST[3:0] = in_1[14:11];
  //   SRC[3:0] = in_1[14:11]; REG2[3:0] = in_1[13:10]; NULL1 = in_1[10]
endmodule
